# Fritzing sketch anemio_v1 (saved by Fritzing 0.9.3b)

parts:
  Pressure = Adafruit_BMP280
  Ambient_Light = Ambient Light Sensor (TEMT6000 Breakout Board)
  Temperature_+_Humidity_DHT22 = DHT22 Humidity and Temperature Sensor
  J$1 = SMA Antenna Connector [package=sma-edge]
  Compass_+_Accelerometer = Adafruit LSM303DLHC Triple-axis Accelerometer+Magnetometer (Compass) [part_number="Adafruit #1120"]
  RF_Comms = Adafruit RFM69HCW Transceiver Radio [part_number="Adafruit #3070 and #3071"]
  Part1 = Arduino Mega 2560 (Rev3)
  IC1 = 10-BIT PROGRAMMABLE MAGNETIC ROTARY ENCODER [package=ssop16]
  Rain_Sensor = Soil Moisture Sensor
  R3 = Resistor [tolerance=±1% resistance=10k package="0603 [SMD]"]
  Water_Temperature_Sensor = Temperature Sensor (Thermistor) [thermistor_type=NTC package=THT]
  LED1 = RGB LED (com. cathode, rgb) [package="5 mm [THT]"]
  R4 = Resistor [tolerance=±1% resistance=50k package="1206 [SMD]"]
  R1 = Resistor [tolerance=±1% resistance=10k package="0402 [SMD]"]
  RF_Comms1 = Adafruit RFM69HCW Transceiver Radio [part_number="Adafruit #3070 and #3071"]
  Raspberry_Pi_Zero1 = Raspberry Pi Zero
  J$2 = SMA Antenna Connector [package=sma-edge]

nets:
  VIN: Pressure.VIN, Pressure.SDO/ADR, Pressure.CS, Ambient_Light.VCC, Temperature_+_Humidity_DHT22.VDD, Compass_+_Accelerometer.VIN, RF_Comms.VIN, Part1.5V, IC1.T_B_1, IC1.VDD3V3, IC1.VDD5V, Rain_Sensor.VCC, R4.Pin_1, R1.Pin_0
  GND: Pressure.GND, Ambient_Light.GND, Temperature_+_Humidity_DHT22.GND, Compass_+_Accelerometer.GND, RF_Comms.GND, Part1.GND, IC1.VSS, Rain_Sensor.GND, Water_Temperature_Sensor.pin_1, LED1.red_anode
  N1: Pressure.SCK/SCL, Compass_+_Accelerometer.SCL, Part1.D21/SCL
  N2: Pressure.SDI/SDA, Compass_+_Accelerometer.SDA, Part1.D20/SDA
  N3: Ambient_Light.S, Part1.A2, R4.Pin_0
  N4: Temperature_+_Humidity_DHT22.DATA, Part1.D22, R1.Pin_1
  N5: J$1.GND, RF_Comms.DIO1
  N6: J$1.SIGNAL, RF_Comms.ANTENNA
  N7: RF_Comms.DIO0, Part1.D2_PWM
  N8: RF_Comms.SCK, Part1.D52
  N9: RF_Comms.MISO, Part1.D50
  N10: RF_Comms.MOSI, Part1.D51
  N11: RF_Comms.CS, Part1.D53
  N12: RF_Comms.RST, Part1.D49
  N13: Part1.A1, Rain_Sensor.SIG
  N14: Part1.A3, LED1.green_anode
  N15: Part1.A4, LED1.blue_anode
  N16: Part1.A5, R3.Pin_0
  N17: Part1.VIN, LED1.common_cathode
  N18: Part1.D7_PWM, IC1.CLK
  N19: Part1.D28, R3.Pin_1, Water_Temperature_Sensor.pin_0
  N20: Part1.D32, IC1.CSN
  N21: Part1.D33, IC1.D0
  N22: RF_Comms1.DIO1, J$2.GND
  N23: RF_Comms1.ANTENNA, J$2.SIGNAL
  VIN_2: RF_Comms1.VIN, Raspberry_Pi_Zero1.5V
  GND_2: RF_Comms1.GND, Raspberry_Pi_Zero1.GND
  N24: RF_Comms1.DIO0, Raspberry_Pi_Zero1.GPIO24
  N25: RF_Comms1.SCK, Raspberry_Pi_Zero1.GPIO11
  N26: RF_Comms1.MISO, Raspberry_Pi_Zero1.GPIO9
  N27: RF_Comms1.MOSI, Raspberry_Pi_Zero1.GPIO10
  N28: RF_Comms1.CS, Raspberry_Pi_Zero1.GPIO8
  N29: RF_Comms1.RST, Raspberry_Pi_Zero1.GPIO5

notes:
  BMP280 can take 3.3 - 5v. 3Vo can output 3volts (up to 100mA)
  This is just a placeholder for the actual rain sensor which works very much the same way as this moisture sensor.
  This is Wind Sensor representation. Pins are (left to right) GND, 12V, OUT, TMP
  WEATHER STATION
  BASE STATION / SERVER

custom parts:
  Adafruit_BMP280: Bosch has stepped up their game with their new BMP280 sensor, an environmental sensor with temperature, barometric pressure that is the next generation upgrade to the BMP085/BMP180/BMP183. This sensor is great for all sorts of weather sensing and can even be used in both I2C and SPI! This precision sensor from Bosch is the best low-cost, precision sensing solution for measuring barometric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
  Adafruit LSM303DLHC Triple-axis Accelerometer+Magnetometer (Compass): He told you "Go West, young maker!" - but you don't know which way is West! Ah, if only you had this triple-axis accelerometer/magnetometer compass module. Inside are two sensors, one is a classic 3-axis accelerometer, which can tell you which direction is down towards the Earth (by measuring gravity). The other is a magnetometer that can sense where the strongest magnetic force is coming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
  Adafruit RFM69HCW Transceiver Radio: Sending data over long distances is like magic, and now you can be a magician with this range of powerful and easy-to-use radio modules. Sure, sometimes you want to talk to a computer (a good time to use WiFi) or perhaps communicate with a Phone (choose Bluetooth Low Energy!) but what if you want to send data very far? Most WiFi, Bluetooth, Zigbee and other wireless chipsets use 2.4GHz, which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
  10-BIT PROGRAMMABLE MAGNETIC ROTARY ENCODER: 10-BIT PROGRAMMABLE MAGNETIC ROTARY ENCODER Source: www.austriamicrosystems.com .. AS5040DataSheetRev12.pdf
